# Fritzing sketch AzureSmartSnoozeAlarmClock (saved by Fritzing 0.9.3b)
breadboards: 2

parts:
  J1 = Piezo Speaker
  Q1 = NPN-Transistor [package="TO92 [THT]"]
  S1 = SWITCH-MOMENTARY-2 [package=tactile-pth-12mm]
  S2 = SWITCH-MOMENTARY-2 [package=tactile-pth-12mm]
  OLED_I2C1 = OLED 128x64 I2C Monochrome Display
  R2 = Resistor [tolerance=±1% resistance=4.7k package=THT]
  R4 = Resistor [tolerance=±1% resistance=4.7k package=THT]
  R1 = Resistor [tolerance=±1% resistance=680 package=THT]
  R3 = Resistor [tolerance=±1% resistance=10k package=THT]

nets:
  N1: J1.pin1, Q1.C
  N2: Q1.E, R3.Pin_1
  N3: Q1.B, R1.Pin_0, R3.Pin_0
  N4: S1.1, R2.Pin_1
  N5: S2.1, R4.Pin_1
  N6: OLED_I2C1.VDD, R4.Pin_0

notes:
  This is for Click Board 1
  This is for Click Board 2
  5V
  3.3V
  GND
  PWM
  AN
  SDA
  SCL
